# Fritzing sketch Raspberry_rele (saved by Fritzing 0.9.3b)

parts:
  WeMos_D1_Mini_Relay_Shield_V1 = WeMos D1 Mini Relay Shield V2
  Raspberry_Pi_1 = Raspberry Pi 3 [part_number=RPI-3-V1.2]

nets:
  5V: WeMos_D1_Mini_Relay_Shield_V1.5V, Raspberry_Pi_1.5V
  N1: WeMos_D1_Mini_Relay_Shield_V1.D1, Raspberry_Pi_1.GPIO21
  N2: WeMos_D1_Mini_Relay_Shield_V1.G, Raspberry_Pi_1.GND
